# Fritzing sketch Fritzing-Fensterheber (saved by Fritzing 0.9.4)
breadboards: 1

parts:
  U1 = ESP32S-HiLetgo [part_number=ESP32S-HiLetgo]
  RHT1 = Humidity and Temperature Sensor RHT03
  Grove1 = Grove OLED 128x96
  MOTOR1 = 28BYJ-48 Stepper Motor
  ULN2003A_-_Stepper_Driver_Board1 = ULN2003A - Stepper Driver Board [package=board]

nets:
  N1: U1.GPIO33, ULN2003A_-_Stepper_Driver_Board1.IN4
  N2: U1.GPIO25, ULN2003A_-_Stepper_Driver_Board1.IN3
  N3: U1.GPIO26, ULN2003A_-_Stepper_Driver_Board1.IN2
  N4: U1.GPIO27, ULN2003A_-_Stepper_Driver_Board1.IN1
  GND: U1.GND, RHT1.GND_2, Grove1.GND, ULN2003A_-_Stepper_Driver_Board1.GND
  VCC: U1.VIN, RHT1.Vcc, Grove1.VCC, MOTOR1.BLUE, ULN2003A_-_Stepper_Driver_Board1.VCC, ULN2003A_-_Stepper_Driver_Board1.BLUE
  N5: U1.GPIO21, Grove1.SDA
  N6: U1.GPIO22, Grove1.SCL
  N7: U1.GPIO23, RHT1.Data-signal
  N8: MOTOR1.PINK, ULN2003A_-_Stepper_Driver_Board1.PINK
  N9: MOTOR1.RED, ULN2003A_-_Stepper_Driver_Board1.RED
  N10: MOTOR1.ORANGE, ULN2003A_-_Stepper_Driver_Board1.ORANGE
  N11: MOTOR1.YELLOW, ULN2003A_-_Stepper_Driver_Board1.YELLOW

custom parts:
  ESP32S-HiLetgo: HiLetgo ESP-WROOM-32 ESP32 ESP-32S Development Board 2.4GHz Dual-Mode WiFi + Bluetooth Dual Cores Microcontroller The ESP32 integrated with Antenna switches, RF Balun, power amplifiers, low-noise amplifiers, filters, and management modules, and the entire solution occupies the least area of PCB. 2.4 GHz Wi-Fi plus Bluetooth dual-mode chip, with TSMC Ultra-low power consumption 40nm technology,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
  28BYJ-48 Stepper Motor: 28BYJ-48 gear-reduction stepper motor (small)
  ULN2003A - Stepper Driver Board: A common stepper motor driver board based on ULN2003APG darlington array
